# Fritzing sketch ArduinoRobot (saved by Fritzing 0.9.3b)
breadboards: 1

parts:
  Part1 = Arduino Uno (Rev3)  # not connected
  M2 = DC Motor
  BAT1 = Battery Holders [package=battery-aa]
  BAT2 = Battery Holders [package=battery-aa]
  BAT3 = Battery Holders [package=battery-aa]
  BAT4 = Battery Holders [package=battery-aa]
  S1 = H-Bridge with L298N
  BT1 = Bluetooth HC-06u [package=THT]  # not connected
  hc-sr1 = hc-sr04  # not connected
  Part2 = KY-033 Tracing Black White Line Hunting Sensor Module For Arduino  # not connected
  S2 = Pololu QTR-8 Reflectabce Sensor array [package=THT]  # not connected
  M3 = DC Motor

nets:
  N1: M2.pin_1, S1.M2-02
  N2: M2.pin_2, S1.M2-01
  N3: BAT1.-, BAT3.+
  N4: BAT1.+, BAT4.-
  N5: BAT2.-, S1.GND
  N6: BAT2.+, BAT3.-
  N7: BAT4.+, S1.12V
  N8: S1.M1-01, M3.pin_2
  N9: S1.M1-02, M3.pin_1

custom parts:
  H-Bridge with L298N: h-bridge
  Bluetooth HC-06u: Bluetooth HC-06 - face up, pins down 16.5mm x 37.5mm PCB
  KY-033 Tracing Black White Line Hunting Sensor Module For Arduino: Tracing Black White Line Hunting Sensor Module For Arduino Description: This is KY-033 tracking sensor. The KY-033 measures the intensity of infrared radiation and delivers it as an analog output voltage. Features: Operating voltage: 2.5 - 12V(cannot over12V) working current: 18mA-20mA at 5V Enhanced accuracy Documents: http://www.vishay.com/docs/83760/tcrt5000.pdf
